// Logisim project lab10.circ as structural Verilog: 1 circuit, main circuit main
module main (
  input  p,
  input  z,
  output y,
  output s1,
  output s2
);

  wire c_out, m1_out, m2_out, m3_out, m5_out, not_1_out, not_2_out, q1_qn, q2_q, q2_qn, r_out, x1_out, x2_out;

  not not_1 (not_1_out, p);
  not not_2 (not_2_out, z);
  Button c (.out(c_out));
  Button r (.out(r_out));
  xor x1 (x1_out, z, q2_q);
  nand m1 (m1_out, x1_out, not_1_out, q1_qn);
  nand m2 (m2_out, q2_qn, p, not_2_out);
  nand m3 (m3_out, z, p, q1_qn);
  nand m4 (s2, m1_out, m2_out);
  not n1 (s1, m3_out);
  D_Flip_Flop q1 (.D(s1), .clk(c_out), .Qn(q1_qn), .reset(r_out));  // open: Q, preset
  D_Flip_Flop q2 (.D(s2), .clk(c_out), .Q(q2_q), .Qn(q2_qn), .reset(r_out));  // open: preset
  xor x2 (x2_out, p, q2_q);
  nand m5 (m5_out, q1_qn, x2_out);
  not n2 (y, m5_out);
endmodule
