// Logisim project automat.circ as structural Verilog: 1 circuit, main circuit main
module main (
  input  z1,
  input  z0
);

  wire and_1_out, and_2_out, and_3_out, and_4_out, c_out, j_k_ff_1_q, j_k_ff_1_qn, j_k_ff_2_q, j_k_ff_2_qn,
       j_k_ff_3_q, j_k_ff_3_qn, not_1_out, not_2_out, or_1_out, or_2_out, or_3_out, or_4_out, xor_1_out;

  not not_1 (not_1_out, z1);
  not not_2 (not_2_out, z0);
  Button c (.out(c_out));
  and and_1 (and_1_out, not_1_out, not_2_out, j_k_ff_2_q, j_k_ff_3_q);
  J_K_Flip_Flop j_k_ff_1 (
    .J(and_1_out), .K(or_1_out), .clk(c_out), .Q(j_k_ff_1_q), .Qn(j_k_ff_1_qn));  // open: preset, reset
  or or_1 (or_1_out, z1, z0, j_k_ff_2_q, j_k_ff_3_q);
  xor xor_1 (xor_1_out, z1, z0);
  and and_2 (and_2_out, not_1_out, not_2_out, j_k_ff_1_qn, j_k_ff_3_q);
  J_K_Flip_Flop j_k_ff_2 (
    .J(and_2_out), .K(or_2_out), .clk(c_out), .Q(j_k_ff_2_q), .Qn(j_k_ff_2_qn));  // open: preset, reset
  or or_2 (or_2_out, xor_1_out, j_k_ff_3_q);
  and and_3 (and_3_out, z1, z0, j_k_ff_2_q);
  and and_4 (and_4_out, not_1_out, not_2_out, j_k_ff_2_qn);
  or or_3 (or_3_out, z1, z0, j_k_ff_1_qn);
  or or_4 (or_4_out, and_3_out, and_4_out);
  J_K_Flip_Flop j_k_ff_3 (
    .J(or_4_out), .K(or_3_out), .clk(c_out), .Q(j_k_ff_3_q), .Qn(j_k_ff_3_qn));  // open: preset, reset

  // Notes on the sheet:
  //   1
  //   2
  //   3
  //   !1
  //   !2
  //   !3
endmodule
