// Logisim project lab5.circ as structural Verilog: 1 circuit, main circuit main
module main (
  input  z,
  input  in_2,
  input  in_3,
  output y
);

  wire and_1_out, and_2_out, and_3_out, and_4_out, and_5_out, c_out, j_k_ff_1_q, j_k_ff_1_qn, j_k_ff_2_q,
       j_k_ff_2_qn, j_k_ff_3_q, j_k_ff_3_qn, not_1_out, or_1_out, or_2_out, r_out;

  not not_1 (not_1_out, z);
  Button c (.out(c_out));
  Button r (.out(r_out));
  and and_1 (and_1_out, j_k_ff_3_qn, not_1_out);
  and and_2 (and_2_out, z, j_k_ff_3_q, j_k_ff_2_q);
  J_K_Flip_Flop j_k_ff_1 (
    .J(or_1_out), .K(in_2), .clk(c_out), .Q(j_k_ff_1_q), .Qn(j_k_ff_1_qn), .reset(r_out));  // open: preset
  or or_1 (or_1_out, and_1_out, and_2_out);
  J_K_Flip_Flop j_k_ff_2 (
    .J(j_k_ff_3_q), .K(in_3), .clk(c_out), .Q(j_k_ff_2_q), .Qn(j_k_ff_2_qn), .reset(r_out));  // open: preset
  and and_3 (and_3_out, j_k_ff_2_qn, not_1_out);
  and and_4 (and_4_out, j_k_ff_2_q, z);
  and and_5 (and_5_out, z, j_k_ff_1_qn);
  J_K_Flip_Flop j_k_ff_3 (
    .J(and_5_out), .K(or_2_out), .clk(c_out), .Q(j_k_ff_3_q), .Qn(j_k_ff_3_qn), .reset(r_out));  // open: preset
  or or_2 (or_2_out, and_3_out, and_4_out);
  and and_6 (y, j_k_ff_2_q, j_k_ff_3_qn, j_k_ff_1_qn);
endmodule
