// Logisim project lab7.circ as structural Verilog: 1 circuit, main circuit main
module main (
  input  z1,
  input  z2,
  output y1,
  output y2
);

  wire and_1_out, and_2_out, and_3_out, and_4_out, and_5_out, and_6_out, and_7_out, and_8_out, and_9_out,
       and_10_out, and_11_out, and_12_out, and_13_out, and_14_out, and_15_out, and_16_out, not_1_out,
       not_2_out, not_3_out, not_4_out, not_5_out, or_1_out, or_2_out;

  not not_1 (not_1_out, z1);
  not not_2 (not_2_out, z2);
  and and_1 (and_1_out, z1, not_2_out, or_1_out);
  and and_2 (and_2_out, not_2_out, or_1_out, y2);
  and and_3 (and_3_out, not_2_out, or_1_out, or_2_out);
  and and_4 (and_4_out, not_2_out, not_1_out, not_5_out, or_2_out);
  and and_5 (and_5_out, z1, not_2_out, or_2_out);
  and and_6 (and_6_out, not_2_out, not_3_out, or_2_out);
  and and_7 (and_7_out, not_2_out, or_2_out, not_5_out);
  and and_8 (and_8_out, not_3_out, y2, not_1_out, not_2_out);
  and and_9 (and_9_out, not_3_out, not_4_out, z1, not_2_out);
  and and_10 (and_10_out, not_3_out, not_4_out, y2, not_2_out);
  and and_11 (and_11_out, or_1_out, or_2_out, z1, not_2_out);
  and and_12 (and_12_out, or_1_out, or_2_out, y2, not_2_out);
  and and_13 (and_13_out, not_1_out, not_2_out, y2);
  and and_14 (and_14_out, not_5_out, or_2_out);
  and and_15 (and_15_out, or_1_out, or_2_out);
  and and_16 (and_16_out, or_1_out, y2);
  or or_1 (or_1_out, and_1_out, and_2_out, and_3_out, and_4_out);
  not not_3 (not_3_out, or_1_out);
  or or_2 (or_2_out, and_5_out, and_6_out, and_7_out, and_8_out);
  not not_4 (not_4_out, or_2_out);
  or or_3 (y1, and_14_out, and_15_out, and_16_out);
  or or_4 (y2, and_9_out, and_10_out, and_11_out, and_12_out, and_13_out);
  not not_5 (not_5_out, y2);

  // Notes on the sheet:
  //   z1 !z1 !z2
  //   q1 !q1
  //   q2 !q2
  //   q3 !q3
  //   q1
  //   !q1
  //   q2
  //   !q2
  //   q3
  //   !q3
endmodule
